# Fritzing sketch PiCamera (saved by Fritzing 0.9.3b)
breadboards: 1

parts:
  R1 = Rotary Potentiometer (Small) [maximum_resistance=100kΩ package=THT]
  R2 = Rotary Potentiometer (Small) [maximum_resistance=100kΩ package=THT]
  U1 = LCD-16X2 [package=lcd-16x2_noholes]
  Raspberry_Pi_1 = Raspberry Pi 3 [part_number=RPI-3-V1.2]
  U2 = AD654 - Low Cost Monolithic Voltage-to-Frequency Converter [part_number=AD654]
  S1 = Momentary Switch [package=ksa_sealed_tac_switch]
  S2 = Momentary Switch [package=ksa_sealed_tac_switch]
  LED1 = LED - 5mm [color="Red (633nm)" package="5 mm [THT]"]

nets:
  VSS: R1.leg1, R2.leg1, U1.VSS, U1.R_W, U1.K, Raspberry_Pi_1.GND, U2.COMMON, S1.3, S2.3, LED1.anode
  N1: R1.wiper, U2.5V
  VDD: R1.leg2, R2.leg2, U1.VDD, U1.A, Raspberry_Pi_1.5V, U2.V+
  N2: R2.wiper, U1.VO
  N3: U1.RS, Raspberry_Pi_1.GIPO24
  N4: U1.E, Raspberry_Pi_1.GIPO23
  N5: U1.DB4, Raspberry_Pi_1.GIPO17
  N6: U1.DB5, Raspberry_Pi_1.GIPO18
  N7: U1.DB6, Raspberry_Pi_1.GIPO27
  N8: U1.DB7, Raspberry_Pi_1.GIPO22
  N9: Raspberry_Pi_1.GIPO11, U2.CAP
  N10: Raspberry_Pi_1.GIPO13, LED1.cathode
  N11: Raspberry_Pi_1.GIPO19, S2.1
  N12: Raspberry_Pi_1.GIPO26, S1.1
  N13: Raspberry_Pi_1.GIPO8, U2.10V
  N14: Raspberry_Pi_1.GIPO25, U2.STROBE, U2.VBG
